# Fritzing sketch avm_schem (saved by Fritzing 0.8.7b)
breadboards: 1

parts:
  U2 = POT [package=pot_mammoth]
  U3 = POT [package=pot_mammoth]
  U4 = POT [package=pot_mammoth]
  U5 = POT [package=pot_mammoth]
  U6 = POT [package=pot_mammoth]
  Part1 = Arduino Uno (Rev3)

nets:
  N1: U2.S, U3.S, U4.S, U5.S, U6.S, Part1.GND
  N2: U2.A, Part1.A0
  N3: U2.E, U3.E, U4.E, U5.E, U6.E, Part1.5V
  N4: U3.A, Part1.A1
  N5: U4.A, Part1.A2
  N6: U5.A, Part1.A3
  N7: U6.A, Part1.A4/SDA
